# Fritzing sketch MotorDistributorSystem (saved by Fritzing 1.0.1rc)
breadboards: 1

parts:
  Mod1 = Raspberry Pi 4B
  Chip1 = SHIFT REGISTER [package=dil16]
  Chip2 = SHIFT REGISTER [package=dil16]
  J2_Common_Gnd_Bus = Camdenboss CTB0158-4 [part_number=CTB0158-4 package=THT]
  J1_3_3V_Bus = Camdenboss CTB0158-4 [part_number=CTB0158-4 package=THT]
  J3_--_connection_to_Pi = Camdenboss CTB0158-4 [part_number=CTB0158-4 package=THT]  # not connected
  Motor4 = DRV 8825 Stepper Motor Carrier, High Current [part_number="DRV 8825"]
  Motor3 = DRV 8825 Stepper Motor Carrier, High Current [part_number="DRV 8825"]
  Motor1 = DRV 8825 Stepper Motor Carrier, High Current [part_number="DRV 8825"]
  Motor2 = DRV 8825 Stepper Motor Carrier, High Current [part_number="DRV 8825"]
  GX_#4 = Hirose DF13 Series Header [part_number=DF13A-4P-1.25H package=DF13A-4P-1.25H]
  GX_#3 = Hirose DF13 Series Header [part_number=DF13A-4P-1.25H package=DF13A-4P-1.25H]
  GX_#1 = Hirose DF13 Series Header [part_number=DF13A-4P-1.25H package=DF13A-4P-1.25H]
  GX_#2 = Hirose DF13 Series Header [part_number=DF13A-4P-1.25H package=DF13A-4P-1.25H]
  J4_12_GND_(common) = Camdenboss CTB0158-4 [part_number=CTB0158-4 package=THT]
  J4_12V_Bus = Camdenboss CTB0158-4 [part_number=CTB0158-4 package=THT]

nets:
  N1: Mod1.GPIO10, Chip2.SER
  N2: Mod1.GPIO25, Chip2.RCK
  N3: Mod1.GPIO11, Chip1.SCK
  N4: Chip1.QB, Motor1.ENABLE
  N5: Chip1.QC, Motor1.STEP
  N6: Chip1.QD, Motor1.DIRECTION
  N7: Chip1.QE, Motor2.ENABLE
  N8: Chip1.QF, Motor2.STEP
  N9: Chip1.QG, Motor2.DIRECTION
  GND: Chip1.GND, Chip1.G, Chip2.GND, Chip2.G, J2_Common_Gnd_Bus.pin1
  VCC: Chip1.SCL, Chip1.VCC, Chip2.SCL, Chip2.VCC, J1_3_3V_Bus.pin1
  N10: Chip1.SER, Chip2.QH*
  N11: Chip2.QB, Motor4.ENABLE
  N12: Chip2.QC, Motor4.STEP
  N13: Chip2.QD, Motor4.DIRECTION
  N14: Chip2.QE, Motor3.ENABLE
  N15: Chip2.QF, Motor3.STEP
  N16: Chip2.QG, Motor3.DIRECTION
  N17: Motor4.VOLTAGE_ST/_MT, J4_12V_Bus.pin1
  N18: Motor4.GROUND_ST/_MT, J4_12_GND_(common).terminal_2
  N19: Motor4.OUT_2B, GX_#4.1
  N20: Motor4.OUT_2A, GX_#4.2
  N21: Motor4.OUT_1A, GX_#4.3
  N22: Motor4.OUT_1B, GX_#4.4
  N23: Motor3.VOLTAGE_ST/_MT, J4_12V_Bus.pin2
  N24: Motor3.GROUND_ST/_MT, J4_12_GND_(common).pin3
  N25: Motor3.OUT_2B, GX_#3.1
  N26: Motor3.OUT_2A, GX_#3.2
  N27: Motor3.OUT_1A, GX_#3.3
  N28: Motor3.OUT_1B, GX_#3.4
  N29: Motor1.VOLTAGE_ST/_MT, J4_12V_Bus.pin3
  N30: Motor1.GROUND_ST/_MT, J4_12_GND_(common).pin1
  N31: Motor1.OUT_2B, GX_#1.1
  N32: Motor1.OUT_2A, GX_#1.2
  N33: Motor1.OUT_1A, GX_#1.3
  N34: Motor1.OUT_1B, GX_#1.4
  N35: Motor2.VOLTAGE_ST/_MT, J4_12V_Bus.pin4
  N36: Motor2.GROUND_ST/_MT, J4_12_GND_(common).terminal_4
  N37: Motor2.OUT_2B, GX_#2.1
  N38: Motor2.OUT_2A, GX_#2.2
  N39: Motor2.OUT_1A, GX_#2.3
  N40: Motor2.OUT_1B, GX_#2.4

notes:
  Output pins are 1-6 on each 74HC595 chip.
  Chip1 : 1(BL) - Enable, 2(GN)-Step, 3(YE)-Dir for Motor4
  4(BL) - Enable, 5(GN)-Step, 6(YE)-Dir for Motor3
  Chip2 : 1(BL) - Enable, 2(GN)-Step, 3(YE)-Dir for Motor2
  4(BL) - Enable, 5(GN)-Step, 6(YE)-Dir for Motor1
  REMEMBER: Chip2 is UPSIDE DOWN (pin1 at bottom)!!!!!
  GX connectors on side of enclosure
  DRV8825 carrier pins are labeled, NOT numbered
  GND and 12V bus are split left/right on 1 terminal block
  J3, Chip1 and Chip2 are on the brown vero board with the 8825 drivers.
  Source File: MotorDistributorSystem.fzz
  This File: MotorDistributorSystem_schem.jpg
